# Fritzing sketch Wig Sketch (saved by Fritzing 1.0.6)

parts:
  A1 = Raspberry Pi Pico W
  M1 = Grove GSR Sensor
  U3 = TOUCH [package=touch1]
  U4 = TOUCH [package=touch1]
  Driver1 = 28BYJ-48 Driver Module [part_number=ULN2003 package=THT]
  SM1 = 28BYJ-48 Stepper Motor [part_number=28BYJ-48]
  U1 = Battery Holders [package=battery-aa]

nets:
  N1: A1.pin_3, A1.pin_33, A1.pin_38, A1.pin_42, M1.SIG, U1.+
  N2: A1.pin_4, Driver1.IN1
  N3: A1.pin_5, Driver1.IN2
  N4: A1.pin_6, Driver1.IN3
  N5: A1.pin_7, Driver1.IN4
  N6: A1.pin_31, M1.GND
  N7: A1.pin_39, U1.-
  N8: A1.pin_40, M1.NC
  N9: M1.S1, U4.T1
  N10: M1.S2, U3.T1
  N11: Driver1.blue-pin, SM1.blue-pin
  N12: Driver1.pink-pin, SM1.pink-pin
  N13: Driver1.yellow-pin, SM1.yellow-pin
  N14: Driver1.orange-pin, SM1.orange-pin
  N15: Driver1.red-pin, SM1.red-pin

custom parts:
  Raspberry Pi Pico W: Raspberry Pi Pico W. Based around the RP2040 microcontroller the Pico W is a low cost microcontroller device bringing Raspberry Pi quality, cost, and easy of use to the microcontroller space. The areas marked KEEPOUT in pcb silkscreen should not have traces running through them to avoid shorts on a soldered in module!
  Grove GSR Sensor: GSR stands for galvanic skin response, is a method of measuring the electrical conductance of the skin. Strong emotion can cause stimulus to your sympathetic nervous system, resulting more sweat being secreted by the sweat glands.
  28BYJ-48 Driver Module: ULN2003 Driver Module for the 28BYJ-48 Unipolar Stepper Motor LED A - Blue wire - Bottom coil left LED B - Pink wire - Top coil left LED C - Yellow wire - Bottom coil right LED D - Orange wire - Top coil right Common rail - red Connector pins: blue - pink - yellow - orange - red Control pins - IN1 to IN4 Power pins - GND & Vmotor (5-12V) On/Off jumper (if removed, power to motor is cut).
  28BYJ-48 Stepper Motor: Unipolar Stepper Motor 28BYJ-48 Top coil - pink & orange Bottom coil - blue & yellow Common rail - red Connector pins: blue - pink - yellow - orange - red
